# Fritzing sketch simple-measuring-circuit (saved by Fritzing 0.9.1b)
breadboards: 1

parts:
  Part1 = Arduino Uno (Rev3) - ICSP
  R1 = Resistor [tolerance=±5% resistance=470 package="1206 [SMD]"]
  Figaro_TGS_2600_Gas_Sensor = Figaro TGS 2602 Gas Sensor

nets:
  N1: Part1.A0, R1.Pin_0, Figaro_TGS_2600_Gas_Sensor.pin_2
  N2: Part1.5V, Figaro_TGS_2600_Gas_Sensor.pin_3, Figaro_TGS_2600_Gas_Sensor.pin_4
  N3: Part1.GND, R1.Pin_1, Figaro_TGS_2600_Gas_Sensor.pin_1

custom parts:
  Figaro TGS 2602 Gas Sensor: The sensing element is comprised of a metal oxide semiconductor layer formed on the alumina substrate of a sensing chip together with an integrated heater. In the presence of detectable gas, sensor conductivity increases depending on gas concentration in the air. A simple electrical circuit can convert the change in conductivity to an output signal which corresponds to the gas concentration.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
